# Fritzing sketch loadcellclg (saved by Fritzing 0.9.3b)
circuit board: 31.2861cm x 15.0137cm
breadboards: 1

parts:
  U1 = NodeMCU V1.0
  LCM1602_IIC1 = LCM1602 IIC [part_number="LCM1602 IIC" chip_label="LCM1602 IIC" package="DIP (Dual Inline) [THT]"]
  LCD1 = LCD screen
  Load_Cell1 = Load Cell - Red/white/black/green
  Part1 = HX711 Weighing Sensor Module
  S1 = Momentary Switch [package=ksa_sealed_tac_switch]  # not connected

nets (from the breadboard view):
  N1: U1.D1, LCM1602_IIC1.SCL
  N2: U1.D2, LCM1602_IIC1.SDA
  N3: U1.D5, Part1.CK/TX
  N4: U1.D6, Part1.DO/RX
  N5: LCM1602_IIC1.VSS, LCD1.LED-
  N6: LCM1602_IIC1.VDD, LCD1.LED+
  N7: LCM1602_IIC1.V0, LCD1.DB7
  N8: LCM1602_IIC1.RS, LCD1.DB6
  N9: LCM1602_IIC1.RW, LCD1.DB5
  N10: LCM1602_IIC1.E, LCD1.DB4
  N11: LCM1602_IIC1.D0, LCD1.DB3
  N12: LCM1602_IIC1.D1, LCD1.DB2
  N13: LCM1602_IIC1.D2, LCD1.DB1
  N14: LCM1602_IIC1.D3, LCD1.DB0
  N15: LCM1602_IIC1.D4, LCD1.E
  N16: LCM1602_IIC1.D5, LCD1.R/W
  N17: LCM1602_IIC1.D6, LCD1.RS
  N18: LCM1602_IIC1.D7, LCD1.V0
  N19: LCM1602_IIC1.A, LCD1.VDD
  N20: LCM1602_IIC1.K, LCD1.VSS
  GND: LCM1602_IIC1.GND, Part1.GND
  VCC: LCM1602_IIC1.VCC, Part1.VCC
  N21: Load_Cell1.wire1, Part1.E+
  N22: Load_Cell1.wire2, Load_Cell1.wire4, Part1.A-
  N23: Load_Cell1.wire3, Part1.E-

custom parts:
  NodeMCU V1.0: ESP8266 based NodeMCU
  LCM1602 IIC: I2C-Module to use a 1602 or 2004 LCD on with the wire.h libory Serial LCD Modul
  Load Cell - Red/white/black/green: A rectangle load cell/weighting pressure Sensor with four wires - Red, white, black, green. Normally corresponding with E+, E-, A+, A- respectively.
  HX711 Weighing Sensor Module: HX711 is a precision 24-bit analog-to-digital converter (ADC) designed for weigh scales and industrial control applications to interface directly with a bridge sensor.

// code stored in the sketch: clgloadcell.ino
// Calibrating the load cell
#include <Arduino.h>
#include "HX711.h"
#include <Wire.h>
int button = 2; // push button is connected
#include <LiquidCrystal_I2C.h>
LiquidCrystal_I2C lcd(0x27,16,2); //set the LCD address to 0x27 for a 16 chars and 2 line display
// HX711 circuit wiring
const int DOUT_PIN = 12;
const int SCK_PIN = 13;
long reading; // global
float finalcalib; // gloabl for global calibration
int knownweight = 200 ; // supplied weight to be calibrated
int temp = 0;    // temporary variable for reading the button pin status
uint32_t start, stop;
volatile float weight;


HX711 scale;


void setup() {
  Serial.begin(115200);
  pinMode(button, INPUT_PULLUP); // declare push button as input
  scale.begin(DOUT_PIN,SCK_PIN);
scale.tare();
  lcd.init();
  lcd.backlight();


  // Print a welcome message to the LCD
  lcd.setCursor(0, 0);
  lcd.print("IOT WEIGHT");
  lcd.setCursor(0, 1);
  lcd.print("LoadCell Test");
  
  delay(5000);
}
void calibration () // calibration test
{
Serial.print(" Enter the Known weight ");
int knownweight = Serial.parseInt();
if (scale.is_ready()) {
    scale.set_scale(); 
    lcd.clear();
  lcd.setCursor(0, 0);
  lcd.print("remove weights  ");   
    Serial.println("Tare... remove any weights from the scale.");
    delay(10000);
    scale.tare();
    lcd.clear();
  lcd.setCursor(0, 0);
  lcd.print(" Tare Done: ");
    Serial.println("Tare done...");
    lcd.clear();
  lcd.setCursor(0, 0);
  lcd.print(" Place known ");
  lcd.setCursor(0,1);
  lcd.print("Weights : ");
    Serial.print("Place a known weight on the scale...");
    delay(10000);
    reading = scale.get_units(10);
    lcd.clear();
  lcd.setCursor(0, 0);


  lcd.print("Results");
   lcd.setCursor(0, 1);
   lcd.print(reading);
   
    Serial.print("Result: ");
    Serial.println(reading);
    delay(9000);
        finalcalib = reading/knownweight;
  } 
  else {
    lcd.clear();
  lcd.setCursor(0, 0);


  lcd.print("HX711 not found");
    Serial.println("HX711 not found.");
  }
  delay(1000);
}


void tare()
{
scale.tare();
    lcd.clear();
  lcd.setCursor(0, 0);
  lcd.print(" Tare Done: ");
    Serial.println("Tare done...");
    lcd.clear();
    delay(5000);


}
void readingsetup()
{
  scale.tare();
  lcd.init();
  lcd.backlight();


  // Print a welcome message to the LCD
  lcd.setCursor(0, 0);
  lcd.print("IOT Weighing");
  lcd.setCursor(0, 1);
  lcd.print("LoadCell Test");


  delay(6000);
 
    scale.begin(DOUT_PIN,SCK_PIN);
  // calib = reading / kown weight 
  // TODO find a nice solution for this calibration..
  // load cell factor 20 KG
  // scale.set_scale(127.15);
  // load cell factor 5 KG
  float calib= finalcalib;
  scale.set_scale(calib);       // TODO you need to calibrate this yourself.
  // reset the scale to zero = 0
  scale.tare();
}
void scalereading() // scale will test reading
{
weight = scale.get_units(5);
   weight= 10*weight;
  // Print the weight reading to the serial monitor
  Serial.print("Weight: ");
  Serial.println(weight);


  // Print the weight reading to the LCD
  lcd.clear();
  lcd.setCursor(0, 0);
  lcd.print("Weight: ");
  lcd.print(weight, 2);
  lcd.print(" g");


  delay(500);  
}


void loop() {
  temp = digitalRead(button);
Serial.println(temp);
  delay(100);  
if (temp  == 0 )
{
  
  calibration () ;
}
else if(temp == 1)
{
readingsetup();
scalereading();
}
delay(5000);
}
//calibration factor will be the (reading)/(known weight)
